# Fritzing sketch sensor_node_github (saved by Fritzing 0.9.3b)

parts:
  PIR1 = PIR sensor
  DHT1 = DHT22 Humidity and Temperature Sensor
  LED1 = RGB LED (com. cathode, rbg) [package="5 mm [THT]"]
  Part1 = Ambient Light Sensor (TEMT6000 Breakout Board)
  U1 = NodeMCU V1.0

nets:
  VDD: PIR1.VDD, U1.Vin
  N1: PIR1.SIG, U1.D5
  GND: PIR1.GND, DHT1.GND, LED1.common_cathode, Part1.GND, U1.GND
  VDD_2: DHT1.VDD, Part1.VCC, U1.3V3
  N2: DHT1.DATA, U1.D7
  N3: LED1.red_anode, U1.D1
  N4: LED1.blue_anode, U1.D2
  N5: LED1.green_anode, U1.D3
  N6: Part1.S, U1.A0

custom parts:
  NodeMCU V1.0: ESP8266 based NodeMCU
