# Fritzing sketch sensor_node_v3 (saved by Fritzing 0.9.3b)
breadboards: 1
perfboards: 1

parts:
  PIR1 = PIR sensor
  R1 = Photocell (LDR) [package=THT]
  LED1 = RGB LED (com. cathode, rbg) [package="5 mm [THT]"]
  DHT1 = DHT22 Humidity and Temperature Sensor
  U1 = NodeMCU V1.0
  R4 = Resistor [tolerance=±5% resistance=10k package="0603 [SMD]"]
  R3 = Resistor [tolerance=±5% resistance=10k package="0603 [SMD]"]

nets:
  VDD: PIR1.VDD, R1.pin_0, DHT1.VDD, U1.3V3, R3.Pin_0
  N1: PIR1.SIG, U1.D4
  GND: PIR1.GND, LED1.common_cathode, DHT1.GND, U1.GND, R4.Pin_0
  N2: R1.pin_1, U1.A0, R4.Pin_1
  N3: LED1.red_anode, U1.D0
  N4: LED1.blue_anode, U1.D1
  N5: LED1.green_anode, U1.D2
  N6: DHT1.DATA, U1.D6, R3.Pin_1

custom parts:
  NodeMCU V1.0: ESP8266 based NodeMCU
