# Fritzing sketch bruh_blinds_v3_final (saved by Fritzing 0.9.3b)

parts:
  U1 = NodeMCU V1.0
  X1 = X113647 Stepper Driver Board [package=board]
  MOTOR1 = 28BYJ-48 Stepper Motor  # not connected
  GY1 = MPU-6050 Board GY-521 [form="♀ (female)" package=THT]

nets:
  N1: U1.D2, GY1.pin3
  N2: U1.D3, GY1.pin4
  N3: U1.D4, X1.IN1
  N4: U1.3V3, GY1.pin1
  N5: U1.GND, GY1.pin2
  N6: U1.D5, X1.IN2
  N7: U1.D6, X1.IN3
  N8: U1.D7, X1.IN4

custom parts:
  NodeMCU V1.0: ESP8266 based NodeMCU
  X113647 Stepper Driver Board: A common stepper motor driver board based on ULN2003APG darlington array
  28BYJ-48 Stepper Motor: 28BYJ-48 gear-reduction stepper motor (small)
  MPU-6050 Board GY-521: Acelerometro y Giroscopio MPU-6050 Board GY-521
